# Fritzing sketch ArduinoMega_3model_NRF_3A4988 (saved by Fritzing 0.9.3b)
breadboards: 1

parts:
  Part1 = Arduino Mega 2560 (Rev3)
  NRF = NRF24L01+ Breakout Board
  A4988 = Pololu A4988 [package=SO16]
  A4988_2 = Pololu A4988 [package=SO16]
  A4988_3 = Pololu A4988 [package=SO16]
  12V = 2.1mm DC Barrel Jack
  C2 = Electrolytic Capacitor [capacitance=100µF package="200 mil [THT, electrolytic]"]
  M2 = Stepper Motor - Bipolar
  M3 = Stepper Motor - Bipolar
  M4 = Stepper Motor - Bipolar
  J1 = Basic Servo

nets:
  N1: Part1.D9_PWM, J1.pulse
  N2: Part1.D8_PWM, A4988.ENABLE, A4988_2.ENABLE, A4988_3.ENABLE
  3V3: Part1.3V3, NRF.VCC
  VDD: Part1.5V, A4988.RESET, A4988.SLEEP, A4988.VDD, A4988_2.RESET, A4988_2.SLEEP, A4988_2.VDD, A4988_3.RESET, A4988_3.SLEEP, A4988_3.VDD, J1.vcc
  GND: Part1.GND, NRF.GND, A4988.GND#8, A4988_2.GND#8, A4988_3.GND#8, J1.gnd
  N3: Part1.D2_PWM, A4988.STEP
  N4: Part1.D3_PWM, A4988_2.STEP
  N5: Part1.D4_PWM, A4988_3.STEP
  N6: Part1.D5_PWM, A4988.DIR
  N7: Part1.D6_PWM, A4988_2.DIR
  N8: Part1.D7_PWM, A4988_3.DIR
  N9: Part1.D49, NRF.CE
  N10: Part1.D50, NRF.MISO
  N11: Part1.D51, NRF.MOSI
  N12: Part1.D52, NRF.SCK
  N13: Part1.D53, NRF.CS
  N14: A4988.1B, M4.D
  N15: A4988.1A, M4.B
  N16: A4988.2A, M4.C
  N17: A4988.2B, M4.A
  N18: A4988.GND#14, A4988_2.GND#14, A4988_3.GND#14, 12V.sleeve, C2.-
  N19: A4988.VMOT, A4988_2.VMOT, A4988_3.VMOT, 12V.center, C2.+
  N20: A4988_2.1B, M3.D
  N21: A4988_2.1A, M3.B
  N22: A4988_2.2A, M3.C
  N23: A4988_2.2B, M3.A
  N24: A4988_3.1B, M2.D
  N25: A4988_3.1A, M2.B
  N26: A4988_3.2A, M2.C
  N27: A4988_3.2B, M2.A

custom parts:
  2.1mm DC Barrel Jack: 2.1mm DC Barrel Jack with Thru-Hole Connectors (breadboardable)
